# Fritzing sketch project (saved by Fritzing 0.9.10b)
breadboards: 1

parts:
  Mod1 = Raspberry Pi Pico
  Part1 = Adafruit RFM69HCW Transceiver Radio [part_number="Adafruit #3070 and #3071"]
  Part2 = Adafruit Ultimate GPS v3 [part_number="Adafruit #746"]
  S1 = Momentary Switch [package=ksa_sealed_tac_switch]
  LED1 = LED - 3mm [color="Red (633nm)" current=0.030 package="3 mm [THT]"]
  J1 = Piezo Speaker
  R1 = Resistor [tolerance=±5% resistance=1k package="2512 [SMD]"]

nets:
  N1: Mod1.pin_1, Part1.MISO
  N2: Mod1.pin_2, Part1.CS
  GND: Mod1.pin_3, Mod1.pin_8, Mod1.pin_13, Mod1.pin_18, Mod1.pin_23, Mod1.pin_28, Mod1.pin_33, Mod1.pin_38, Mod1.pin_42, Part1.GND, Part2.GND, LED1.cathode, J1.pin1
  N3: Mod1.pin_4, Part1.SCK
  N4: Mod1.pin_5, Part1.MOSI
  N5: Mod1.pin_6, Part1.RST
  N6: Mod1.pin_16, Part2.RX
  N7: Mod1.pin_17, Part2.TX
  N8: Mod1.pin_19, R1.Pin_0
  N9: Mod1.pin_20, S1.3
  VIN: Mod1.pin_36, Part1.VIN, Part2.VIN, S1.2
  N10: LED1.anode, J1.pin2, R1.Pin_1

custom parts:
  Raspberry Pi Pico: Raspberry Pi Pico. Based around the RP2040 microcontroller the Pico is a low cost microcontroller device bringing Raspberry Pi quality, cost, and easy of use to the microcontroller space. Jan 2021, Split part in to two versions: tht (this one) and SMD. This one will drill holes for a .1 in header in pcb to allow plugging in the module as well as providing pads to solder the module to the top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
  Adafruit RFM69HCW Transceiver Radio: Sending data over long distances is like magic, and now you can be a magician with this range of powerful and easy-to-use radio modules. Sure, sometimes you want to talk to a computer (a good time to use WiFi) or perhaps communicate with a Phone (choose Bluetooth Low Energy!) but what if you want to send data very far? Most WiFi, Bluetooth, Zigbee and other wireless chipsets use 2.4GHz, which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
  Adafruit Ultimate GPS v3: We carry a few different GPS modules here in the Adafruit shop, but none that satisfied our every desire - that's why we designed this little GPS breakout board. We believe this is the Ultimate GPS module, so we named it that. It's got everything you want and more: -165 dBm sensitivity, 10 Hz updates, 66 channels 5V friendly design and only 20mA current draw Breadboard friendly + two mounting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
